// Logisim project 01.circ as structural Verilog: 1 circuit, main circuit main
module main (
  input  P,
  input  Q,
  input  R,
  input  S,
  output F_P_Q_R_S_prime__QRS_prime
);

  wire n7404_1_p3, n7408_1_p2, n7408_1_p3, n7408_1_p6, n7408_1_p11, n7432_1_p3;

  // _7404 7404_1: pin names not known; wires that end beside it: 1'b1, S, n7404_1_p3, 1'b0, 1'b1
  // _7408 7408_1: pin names not known; wires that end beside it: P, n7408_1_p2, n7408_1_p3, Q, R, n7408_1_p6, 1'b0, 1'b1, n7408_1_p6, n7404_1_p3, n7408_1_p11
  // _7432 7432_1: pin names not known; wires that end beside it: Q, R, n7432_1_p3, n7432_1_p3, n7404_1_p3, n7408_1_p2, 1'b0, 1'b1, n7408_1_p11, n7408_1_p3, F_P_Q_R_S_prime__QRS_prime, 1'b0
endmodule
