// Logisim project 02.circ as structural Verilog: 1 circuit, main circuit main
module main (
  input  A,
  input  B,
  input  C,
  output X,
  output Z,
  output Y
);

  wire n7404_1_p3, n7404_1_p5, n7404_1_p7, n7404_1_p11, n7432_1_p3, n7432_1_p6, n7432_1_p11, n7432_1_p14;

  // _7404 7404_1: pin names not known; wires that end beside it: 1'b1, A, n7404_1_p3, B, n7404_1_p5, C, n7404_1_p7, 1'b0, 1'b1, Y, n7404_1_p11
  // _7432 7432_1: pin names not known; wires that end beside it: n7404_1_p3, B, n7432_1_p3, A, n7404_1_p5, n7432_1_p6, 1'b0, 1'b1, Y, n7404_1_p7, n7432_1_p11, n7404_1_p11, C, n7432_1_p14
  // _7408 7408_1: pin names not known; wires that end beside it: n7432_1_p3, n7432_1_p6, Y, n7432_1_p11, n7432_1_p14, Z, 1'b0, 1'b1, 1'b0

  assign X = A;

  // Notes on the sheet:
  //   AB'+A'B
endmodule
