// Logisim project 1905072.circ as structural Verilog: 1 circuit, main circuit main
module main (
  input  P,
  input  Q,
  input  R,
  input  S,
  output F
);

  wire n7432_1_p4, n7432_1_p7;

  // _7432 7432_1: pin names not known; wires that end beside it: 1'b1, P, Q, n7432_1_p4, R, S, n7432_1_p7, 1'b0, 1'b1
  // _7408 7408_1: pin names not known; wires that end beside it: n7432_1_p4, n7432_1_p7, F, 1'b0, 1'b1, 1'b0
endmodule
