// Logisim project Practice.circ as structural Verilog: 2 circuits, main circuit main
module main (
  input  D,
  input  C,
  input  B,
  input  A,
  output out_5
);

  wire n7404_1_p2, n7404_1_p4, n7404_1_p8, n7404_1_p10, n7421_1_p5, n7421_1_p12, n7421_2_p5, n7421_2_p12,
       n7421_3_p5, n7421_3_p12, n7421_4_p5, n7421_4_p12, n7432_1_p3, n7432_1_p6, n7432_1_p11, n7432_1_p14,
       n7432_2_p3, n7432_2_p6;

  // _7404 7404_1: pin names not known; wires that end beside it: A, n7404_1_p2, B, n7404_1_p4, 1'b0, 1'b1, C, n7404_1_p8, D, n7404_1_p10
  // _7421 7421_1: pin names not known; wires that end beside it: n7404_1_p2, n7404_1_p4, n7404_1_p8, n7404_1_p10, n7421_1_p5, 1'b0, 1'b1, A, B, C, D, n7421_1_p12
  // _7421 7421_2: pin names not known; wires that end beside it: A, B, n7404_1_p8, D, n7421_2_p5, 1'b0, 1'b1, n7404_1_p2, n7404_1_p4, C, n7404_1_p10, n7421_2_p12
  // _7421 7421_3: pin names not known; wires that end beside it: n7404_1_p2, B, n7404_1_p8, D, n7421_3_p5, 1'b0, 1'b1, A, n7404_1_p4, n7404_1_p8, n7404_1_p10, n7421_3_p12
  // _7421 7421_4: pin names not known; wires that end beside it: A, n7404_1_p4, C, n7404_1_p10, n7421_4_p5, 1'b0, 1'b1, n7404_1_p2, B, C, D, n7421_4_p12
  // _7432 7432_1: pin names not known; wires that end beside it: n7421_1_p5, n7421_1_p12, n7432_1_p3, n7421_2_p5, n7421_2_p12, n7432_1_p6, 1'b0, 1'b1, n7421_3_p5, n7421_3_p12, n7432_1_p11, n7421_4_p5, n7421_4_p12, n7432_1_p14
  // _7432 7432_2: pin names not known; wires that end beside it: n7432_1_p3, n7432_1_p6, n7432_2_p3, n7432_1_p11, n7432_1_p14, n7432_2_p6, 1'b0, 1'b1, n7432_2_p3, n7432_2_p6, out_5

  // Notes on the sheet:
  //   A'
  //   B'
  //   C'
  //   D'
endmodule

module Yo (
  input  A,
  input  B,
  input  C,
  input  D,
  output out_5
);

  wire n7404_1_p2, n7404_1_p3, n7404_1_p8, n7404_1_p9, n7404_1_p13, n7404_1_p15, n7404_1_p16, n7404_1_p17,
       n7408_1_p9, n7432_1_p6, n7432_1_p11;

  // _7404 7404_1: pin names not known; wires that end beside it: 1'b1, n7404_1_p2, n7404_1_p3, A, n7404_1_p2, B, n7404_1_p3, n7404_1_p8, n7404_1_p9, 1'b0, 1'b1, C, n7404_1_p13, D, n7404_1_p15, n7404_1_p16, n7404_1_p17, n7404_1_p13, n7404_1_p15
  // _7408 7408_1: pin names not known; wires that end beside it: n7404_1_p17, B, C, n7404_1_p16, 1'b0, 1'b1, D, n7404_1_p2, n7408_1_p9, n7408_1_p9, n7404_1_p9
  // _7432 7432_1: pin names not known; wires that end beside it: C, D, n7404_1_p8, A, n7404_1_p17, n7432_1_p6, 1'b0, 1'b1, n7408_1_p9, n7404_1_p9, n7432_1_p11, n7432_1_p11, n7432_1_p6, out_5, 1'b0

  // Notes on the sheet:
  //   A+(BC)'+DA'+(C+D)'
  //   A'
  //   B'
  //   C'
  //   D'
endmodule
