// Logisim project Project2.circ as structural Verilog: 1 circuit, main circuit main
module main (
  input  A,
  input  B,
  input  C,
  output out_4
);

  wire And_p1, Not_p2, Not_p5, Not_p6;

  // _7404 Not: pin names not known; wires that end beside it: A, Not_p2, 1'b0, 1'b1, Not_p5, Not_p6
  // _7408 And: pin names not known; wires that end beside it: And_p1, Not_p6, out_4, 1'b0, 1'b1, C, A, Not_p5
  // _7432 Or: pin names not known; wires that end beside it: 1'b0, 1'b1, Not_p2, B, And_p1

  // Notes on the sheet:
  //   (A'+B)(CA)'
endmodule
