// Logisim project ct4.circ as structural Verilog: 1 circuit, main circuit hjh
module hjh (
  output y1,
  output y2,
  output y3,
  output Lock_Open,
  output Alarm
);

  wire A_out, and_1_out, and_2_out, and_3_out, and_4_out, and_5_out, and_6_out, and_7_out, and_8_out,
       and_10_out, and_11_out, B_out, d_ff_1_qn, d_ff_2_qn, d_ff_3_qn, nor_1_out, or_1_out, or_2_out,
       or_3_out;

  Button B (.out(B_out));
  Button A (.out(A_out));
  nor nor_1 (nor_1_out, B_out, A_out);
  and and_1 (and_1_out, B_out, d_ff_2_qn, y1);
  and and_2 (and_2_out, B_out, d_ff_3_qn);
  and and_3 (and_3_out, A_out, d_ff_1_qn, y2, d_ff_3_qn);
  and and_4 (and_4_out, B_out, d_ff_2_qn, y3);
  and and_5 (and_5_out, B_out, y1, y2, d_ff_3_qn);
  and and_6 (and_6_out, A_out, d_ff_1_qn, d_ff_3_qn);
  and and_7 (and_7_out, B_out, y2, d_ff_3_qn);
  and and_8 (and_8_out, B_out, y1, d_ff_3_qn);
  and and_9 (Lock_Open, B_out, d_ff_1_qn, y2, y3);
  and and_10 (and_10_out, A_out, y1);
  and and_11 (and_11_out, A_out, y3);
  D_Flip_Flop d_ff_1 (.clk(nor_1_out), .D(or_1_out), .Q(y1), .Qn(d_ff_1_qn));  // open: preset, en, reset
  or or_1 (or_1_out, and_1_out, and_2_out);
  D_Flip_Flop d_ff_2 (.clk(nor_1_out), .D(or_2_out), .Q(y2), .Qn(d_ff_2_qn));  // open: preset, en, reset
  or or_2 (or_2_out, and_3_out, and_4_out, and_5_out);
  D_Flip_Flop d_ff_3 (.clk(nor_1_out), .D(or_3_out), .Q(y3), .Qn(d_ff_3_qn));  // open: preset, en, reset
  or or_3 (or_3_out, and_6_out, and_7_out, and_8_out);
  or or_4 (Alarm, and_10_out, and_11_out);

  // Notes on the sheet:
  //   ABAB to open
  //   BBBBB to reset
endmodule
