// Logisim project 1905072-1.circ as structural Verilog: 1 circuit, main circuit JK
module JK (
  input  Initial_Input,
  input  J,
  input  K,
  output Q,
  output Q_prime
);

  wire CLK_out, n7400_1_p3, n7400_1_p4, n7400_1_p12, n7400_2_p3, n7400_2_p6, n7410_1_p6, n7410_1_p10;

  Clock CLK (.out(CLK_out));
  // _7410 7410_1: pin names not known; wires that end beside it: J, CLK_out, CLK_out, Q, K, n7410_1_p6, 1'b0, 1'b1, Q_prime, n7410_1_p10
  // _7400 7400_1: pin names not known; wires that end beside it: Initial_Input, n7410_1_p10, n7400_1_p3, n7400_1_p4, n7400_1_p4, n7410_1_p6, n7400_1_p3, 1'b0, 1'b1, CLK_out, CLK_out, n7400_1_p12
  // _7400 7400_2: pin names not known; wires that end beside it: n7400_1_p4, n7400_1_p12, n7400_2_p3, n7400_1_p12, n7400_1_p3, n7400_2_p6, 1'b0, 1'b1, n7400_2_p3, Q_prime, Q, Q, n7400_2_p6, Q_prime

  // Notes on the sheet:
  //   J
  //   0
  //   0
  //   1
  //   1
  //   Qn+1
  //   K
  //   Qn
  //   0
  //   1
  //   0
  //   1
  //   Qn'
  //   0
  //   1
endmodule
