// Logisim project 1905072-2.circ as structural Verilog: 1 circuit, main circuit 4BitUniversalShiftRegister
module _4BitUniversalShiftRegister (
  input  PR,
  input  CLEAR,
  input  IR,
  input  IL,
  input  s1,
  input  s0,
  input  I3,
  input  I2,
  input  I1,
  input  I0,
  output A3,
  output A2,
  output A1,
  output A0
);

  wire CLK_out, n7474_1_p2, n7474_1_p8, n7474_2_p2, n7474_2_p8;

  Clock CLK (.out(CLK_out));
  // _7474 7474_1: pin names not known; wires that end beside it: CLEAR, n7474_1_p2, CLK_out, PR, A3, 1'b1, CLEAR, n7474_1_p8, CLK_out, PR
  // _74153 74153_1: pin names not known; wires that end beside it: 1'b0, 1'b0, s1, I3, A2, IR, A3, n7474_1_p2, 1'b0, A2, 1'b1, 1'b0, s0, I2, A1, A3, A2, n7474_1_p8
  // _7474 7474_2: pin names not known; wires that end beside it: CLEAR, n7474_2_p2, CLK_out, PR, A1, 1'b1, CLEAR, n7474_2_p8, CLK_out, PR
  // _74153 74153_2: pin names not known; wires that end beside it: 1'b0, 1'b0, s1, I1, A0, A2, A1, n7474_2_p2, 1'b0, A0, 1'b1, 1'b0, s0, I0, IL, A1, A0, n7474_2_p8

  // Notes on the sheet:
  //   Serial in for right shift
  //   4 Bit Universal Shift Register
  //   Parallel Output
  //   Parallel Input
  //   S1
  //   0
  //   0
  //   1
  //   1
  //   Serial in for left shift
  //   Mode
  //   S0
  //   0
  //   No Change
  //   1
  //   Right Shift
  //   0
  //   Left Shift
  //   Paralllel Load
  //   1
endmodule
