// Logisim project 1905072-2.circ as structural Verilog: 1 circuit, main circuit 4BitUniversalShiftRegister
module _4BitUniversalShiftRegister (
  input  PR,
  input  CLEAR,
  input  Serial_in_for_Right_Shift,
  input  Serial_in_for_Left_Shift,
  input  s1,
  input  s0,
  input  in_7,
  input  in_8,
  input  in_9,
  input  in_10,
  output out_11,
  output out_12,
  output out_13,
  output out_14
);

  wire CLK_out, n7474_1_p2, n7474_1_p8, n7474_2_p2, n7474_2_p8;

  Clock CLK (.out(CLK_out));
  // _7474 7474_1: pin names not known; wires that end beside it: CLEAR, n7474_1_p2, CLK_out, PR, out_11, 1'b1, CLEAR, n7474_1_p8, CLK_out, PR
  // _74153 74153_1: pin names not known; wires that end beside it: 1'b0, 1'b0, s1, in_7, out_12, Serial_in_for_Right_Shift, out_11, n7474_1_p2, 1'b0, out_12, 1'b1, 1'b0, s0, in_8, out_13, out_11, out_12, n7474_1_p8
  // _7474 7474_2: pin names not known; wires that end beside it: CLEAR, n7474_2_p2, CLK_out, PR, out_13, 1'b1, CLEAR, n7474_2_p8, CLK_out, PR
  // _74153 74153_2: pin names not known; wires that end beside it: 1'b0, 1'b0, s1, in_9, out_14, out_12, out_13, n7474_2_p2, 1'b0, out_14, 1'b1, 1'b0, s0, in_10, Serial_in_for_Left_Shift, out_13, out_14, n7474_2_p8

  // Notes on the sheet:
  //   4 Bit Universal Shift Register
  //   Parallel Output
  //   Parallel Input
  //   S1
  //   0
  //   0
  //   1
  //   1
  //   Mode
  //   S0
  //   0
  //   No Change
  //   1
  //   Right Shift
  //   0
  //   Left Shift
  //   Paralllel Load
  //   1
endmodule
