// Logisim project FlipFlop.circ as structural Verilog
module main (
  input  S,
  input  J,
  input  K,
  input  R,
  input  S_2,
  input  J_2,
  input  R_2,
  input  K_2,
  input  in_9,
  input  in_10,
  input  D,
  input  T,
  input  in_13,
  output Q_prime,
  output Q_prime_2,
  output Q,
  output Q_2,
  output Q_3,
  output Q_4,
  output Q_prime_3,
  output Q_prime_4,
  output Q_5,
  output Q_prime_5,
  output Q_6,
  output Q_7,
  output Q_prime_6,
  output Q_prime_7
);

  wire and_1_out, and_2_out, and_3_out, and_4_out, clock_1_out, clock_2_out, clock_3_out, clock_4_out,
       clock_5_out, clock_6_out, clock_7_out, nand_1_out, nand_2_out, nand_3_out, nand_4_out, nand_7_out,
       nand_8_out, nand_9_out, nand_10_out, nand_11_out, nand_14_out, nand_15_out, nand_16_out, nand_17_out,
       nand_20_out, nand_21_out, not_1_out;

  Clock clock_1 (.out(clock_1_out));
  Clock clock_2 (.out(clock_2_out));
  Clock clock_3 (.out(clock_3_out));
  Clock clock_4 (.out(clock_4_out));
  and and_1 (and_1_out, S, clock_1_out);
  and and_2 (and_2_out, clock_1_out, R);
  nand nand_1 (nand_1_out, S_2, clock_2_out);
  nand nand_2 (nand_2_out, clock_2_out, R_2);
  not not_1 (not_1_out, D);
  nand nand_3 (nand_3_out, Q_prime_5, in_9, clock_3_out);
  nand nand_4 (nand_4_out, clock_3_out, Q_5, in_10);
  nor nor_1 (Q_prime, and_1_out, Q);
  nor nor_2 (Q, Q_prime, and_2_out);
  nand nand_5 (Q_3, nand_1_out, Q_prime_3);
  nand nand_6 (Q_prime_3, Q_3, nand_2_out);
  nand nand_7 (nand_7_out, D, clock_4_out);
  nand nand_8 (nand_8_out, clock_4_out, not_1_out);
  nand nand_9 (nand_9_out, nand_3_out, nand_10_out);
  nand nand_10 (nand_10_out, nand_9_out, nand_4_out);
  nand nand_11 (nand_11_out, clock_3_out, clock_3_out);
  nand nand_12 (Q_7, nand_7_out, Q_prime_7);
  nand nand_13 (Q_prime_7, Q_7, nand_8_out);
  Clock clock_5 (.out(clock_5_out));
  Clock clock_6 (.out(clock_6_out));
  nand nand_14 (nand_14_out, nand_9_out, nand_11_out);
  nand nand_15 (nand_15_out, nand_11_out, nand_10_out);
  and and_3 (and_3_out, Q_prime_2, J, clock_5_out);
  and and_4 (and_4_out, clock_5_out, K, Q_2);
  nand nand_16 (nand_16_out, Q_4, clock_6_out);
  nand nand_17 (nand_17_out, clock_6_out, Q_prime_4);
  nand nand_18 (Q_5, nand_14_out, Q_prime_5);
  nand nand_19 (Q_prime_5, Q_5, nand_15_out);
  Clock clock_7 (.out(clock_7_out));
  nand nand_20 (nand_20_out, Q_6, clock_7_out);
  nand nand_21 (nand_21_out, clock_7_out, in_13);
  nor nor_3 (Q_prime_2, and_3_out, Q_2);
  nor nor_4 (Q_2, Q_prime_2, and_4_out);
  nand nand_22 (Q_4, nand_16_out, Q_prime_4);
  nand nand_23 (Q_prime_4, Q_4, nand_17_out);
  nand nand_24 (Q_6, nand_20_out, in_13);
  nand nand_25 (in_13, Q_6, nand_21_out);

  assign Q_prime_6 = in_13;
endmodule

module _2BitBinaryCounter (
  output [1:0] out_1
);

  wire clock_1_out;

  Clock clock_1 (.out(clock_1_out));
  J_K_Flip_Flop j_k_ff_1 (.J(1'b1), .clk(clock_1_out), .K(1'b1), .Q(out_1[0]));  // open: Qn, preset, en, reset
  J_K_Flip_Flop j_k_ff_2 (.J(out_1[0]), .clk(clock_1_out), .K(out_1[0]), .Q(out_1[1]));  // open: Qn, preset, en, reset
endmodule

module SequenceDetector (
  input  x,
  output z,
  output [1:0] out_3
);

  wire and_1_out, and_2_out, clock_1_out, d_ff_1_qn, not_1_out, or_1_out;

  Clock clock_1 (.out(clock_1_out));
  not not_1 (not_1_out, x);
  D_Flip_Flop d_ff_1 (.clk(clock_1_out), .D(not_1_out), .Q(out_3[0]), .Qn(d_ff_1_qn));  // open: preset, en, reset
  and and_1 (and_1_out, out_3[1], not_1_out, d_ff_1_qn);
  and and_2 (and_2_out, x, out_3[0]);
  or or_1 (or_1_out, and_1_out, and_2_out);
  D_Flip_Flop d_ff_2 (.clk(clock_1_out), .D(or_1_out), .Q(out_3[1]));  // open: Qn, preset, en, reset
  and and_3 (z, out_3[1], out_3[0], x);
endmodule

module MasterSlaveJKFlipFlop (
  input  in_1,
  input  J,
  input  K,
  input  in_4,
  input  Initial_Input,
  input  in_6,
  input  in_7,
  output Q,
  output Q_prime,
  output out_10,
  output out_11
);

  wire _7400_1_2_out, _7400_1_3_out, _7400_1_out, _7400_2_2_out, _7400_2_out, _7410_2_out, _7410_out,
       CLK_out, clock_1_out, n7400_1_p3, n7400_1_p4, n7400_1_p12, n7400_2_p3, n7400_2_p6, n7410_1_p6,
       n7410_1_p10;

  Clock CLK (.out(CLK_out));
  nand _7410 (_7410_out, Q_prime, J, CLK_out);
  nand _7410_2 (_7410_2_out, CLK_out, Q, K);
  Clock clock_1 (.out(clock_1_out));
  nand _7400_1 (_7400_1_out, _7410_out, _7400_1_2_out);
  nand _7400_1_2 (_7400_1_2_out, _7400_1_out, _7410_2_out);
  nand _7400_1_3 (_7400_1_3_out, CLK_out, CLK_out);
  // _7410 7410_1: pin names not known; wires that end beside it: in_6, clock_1_out, clock_1_out, out_10, in_7, n7410_1_p6, 1'b0, 1'b1, out_11, n7410_1_p10
  nand _7400_2 (_7400_2_out, _7400_1_out, _7400_1_3_out);
  nand _7400_2_2 (_7400_2_2_out, _7400_1_3_out, _7400_1_2_out);
  // _7400 7400_1: pin names not known; wires that end beside it: Initial_Input, n7410_1_p10, n7400_1_p3, n7400_1_p4, n7400_1_p4, n7410_1_p6, n7400_1_p3, 1'b0, 1'b1, clock_1_out, clock_1_out, n7400_1_p12
  nand _7400_2_3 (Q, _7400_2_out, Q_prime);
  nand _7400_2_4 (Q_prime, Q, _7400_2_2_out);
  // _7400 7400_2: pin names not known; wires that end beside it: n7400_1_p4, n7400_1_p12, n7400_2_p3, n7400_1_p12, n7400_1_p3, n7400_2_p6, 1'b0, 1'b1, n7400_2_p3, out_11, out_10, out_10, n7400_2_p6, out_11

  // Notes on the sheet:
  //   13
  //   1
  //   2
  //   3
  //   4
  //   5
  //   12
  //   6
  //   1
  //   2
  //   4
  //   5
  //   10
  //   9
  //   3
  //   6
  //   8
  //   1
  //   2
  //   4
  //   5
  //   3
  //   13
  //   12
  //   10
  //   6
  //   9
  //   11
  //   8
endmodule

module JK (
  input  Initial_Input,
  input  J,
  input  K,
  output Q,
  output Q_prime
);

  wire CLK_out, n7400_1_p3, n7400_1_p4, n7400_1_p12, n7400_2_p3, n7400_2_p6, n7410_1_p6, n7410_1_p10;

  Clock CLK (.out(CLK_out));
  // _7410 7410_1: pin names not known; wires that end beside it: J, CLK_out, CLK_out, Q, K, n7410_1_p6, 1'b0, 1'b1, Q_prime, n7410_1_p10
  // _7400 7400_1: pin names not known; wires that end beside it: Initial_Input, n7410_1_p10, n7400_1_p3, n7400_1_p4, n7400_1_p4, n7410_1_p6, n7400_1_p3, 1'b0, 1'b1, CLK_out, CLK_out, n7400_1_p12
  // _7400 7400_2: pin names not known; wires that end beside it: n7400_1_p4, n7400_1_p12, n7400_2_p3, n7400_1_p12, n7400_1_p3, n7400_2_p6, 1'b0, 1'b1, n7400_2_p3, Q_prime, Q, Q, n7400_2_p6, Q_prime
endmodule
