// Logisim project Register.circ as structural Verilog: 3 circuits, main circuit main
module main (
  input  in_1,
  input  in_2,
  input  in_3,
  input  in_4,
  input  in_5,
  input  in_6,
  output out_7,
  output out_8,
  output out_9,
  output out_10
);

  wire clock_1_out, clock_2_out, d_ff_1_q, d_ff_3_q, d_ff_5_q;

  Clock clock_1 (.out(clock_1_out));
  Clock clock_2 (.out(clock_2_out));
  D_Flip_Flop d_ff_1 (.clk(clock_1_out), .D(in_2), .Q(d_ff_1_q));  // open: Qn, preset, en, reset
  D_Flip_Flop #(.trigger("high")) d_ff_2 (.clk(clock_2_out), .D(in_3), .Q(out_7));  // open: Qn, preset, en, reset
  D_Flip_Flop d_ff_3 (.clk(clock_1_out), .D(d_ff_1_q), .Q(d_ff_3_q));  // open: Qn, preset, en, reset
  D_Flip_Flop #(.trigger("high")) d_ff_4 (.clk(clock_2_out), .D(in_4), .Q(out_8));  // open: Qn, preset, en, reset
  D_Flip_Flop d_ff_5 (.clk(clock_1_out), .D(d_ff_3_q), .Q(d_ff_5_q));  // open: Qn, preset, en, reset
  D_Flip_Flop #(.trigger("high")) d_ff_6 (.clk(clock_2_out), .D(in_5), .Q(out_9));  // open: Qn, preset, en, reset
  D_Flip_Flop d_ff_7 (.clk(clock_1_out), .D(d_ff_5_q));  // open: Q, Qn, preset, en, reset
  D_Flip_Flop #(.trigger("high")) d_ff_8 (.clk(clock_2_out), .D(in_6), .Q(out_10));  // open: Qn, preset, en, reset
endmodule

module UniversalShiftRegister (
  input  CLEAR,
  input  [1:0] S,
  input  Serial_in_for_Left_Shift,
  input  in_4,
  input  in_5,
  input  in_6,
  input  in_7,
  input  Serial_In_For_Right_Shift,
  output Serial_out_for_left_shift,
  output out_10,
  output out_11,
  output Serial_out_for_right_shift
);

  wire clock_1_out, multiplexer_1_out, multiplexer_2_out, multiplexer_3_out, multiplexer_4_out, n74153_1_p1,
       n74153_1_p3, n74153_1_p8, n74153_1_p9, n74153_2_p1, n74153_2_p8;

  Clock clock_1 (.out(clock_1_out));
  Multiplexer #(.select(2), .enable("false")) multiplexer_1 (
    .in0(Serial_out_for_left_shift), .in1(Serial_In_For_Right_Shift), .in2(out_10), .in3(in_4),
    .out(multiplexer_1_out), .sel(S));
  D_Flip_Flop d_ff_1 (
    .clk(clock_1_out), .D(multiplexer_1_out), .Q(Serial_out_for_left_shift), .reset(CLEAR));  // open: Qn, preset, en
  Multiplexer #(.select(2), .enable("false")) multiplexer_2 (
    .in0(out_10), .in1(Serial_out_for_left_shift), .in2(out_11), .in3(in_5), .out(multiplexer_2_out), .sel(S));
  // _74153 74153_1: pin names not known; wires that end beside it: n74153_1_p1, 1'b0, n74153_1_p3, n74153_1_p1, 1'b0, 1'b1, 1'b0, n74153_1_p8, n74153_1_p9, n74153_1_p9
  D_Flip_Flop d_ff_2 (.clk(clock_1_out), .D(multiplexer_2_out), .Q(out_10), .reset(CLEAR));  // open: Qn, preset, en
  D_Flip_Flop d_ff_3 (.clk(clock_1_out), .D(multiplexer_3_out), .Q(out_11), .reset(CLEAR));  // open: Qn, preset, en
  Multiplexer #(.select(2), .enable("false")) multiplexer_3 (
    .in0(out_11), .in1(out_10), .in2(Serial_out_for_right_shift), .in3(in_6), .out(multiplexer_3_out), .sel(S));
  // _74153 74153_2: pin names not known; wires that end beside it: n74153_2_p1, 1'b0, n74153_1_p3, n74153_2_p1, 1'b0, 1'b1, n74153_1_p8, n74153_2_p8, n74153_2_p8
  Multiplexer #(.select(2), .enable("false")) multiplexer_4 (
    .in0(Serial_out_for_right_shift), .in1(out_11), .in2(Serial_in_for_Left_Shift), .in3(in_7),
    .out(multiplexer_4_out), .sel(S));
  D_Flip_Flop d_ff_4 (
    .clk(clock_1_out), .D(multiplexer_4_out), .Q(Serial_out_for_right_shift), .reset(CLEAR));  // open: Qn, preset, en
endmodule

module _4BitUniversalShiftRegister (
  input  CLEAR,
  input  Serial_in_for_Right_Shift,
  input  Serial_in_for_Left_Shift,
  input  s1,
  input  s0,
  input  in_6,
  input  in_7,
  input  in_8,
  input  in_9,
  output out_10,
  output out_11,
  output out_12,
  output out_13
);

  wire CLK_out, n7474_1_p2, n7474_1_p8, n7474_2_p2, n7474_2_p8;

  Clock CLK (.out(CLK_out));
  // _7474 7474_1: pin names not known; wires that end beside it: CLEAR, n7474_1_p2, CLK_out, out_10, 1'b0, 1'b1, CLEAR, n7474_1_p8, CLK_out, out_11
  // _74153 74153_1: pin names not known; wires that end beside it: 1'b0, s1, in_6, out_11, Serial_in_for_Right_Shift, out_10, n7474_1_p2, 1'b0, 1'b1, 1'b0, s0, in_7, out_12, out_10, out_11, n7474_1_p8
  // _7474 7474_2: pin names not known; wires that end beside it: CLEAR, n7474_2_p2, CLK_out, out_12, 1'b0, 1'b1, CLEAR, n7474_2_p8, CLK_out, out_13
  // _74153 74153_2: pin names not known; wires that end beside it: 1'b0, s1, in_8, out_13, out_11, out_12, n7474_2_p2, 1'b0, 1'b1, 1'b0, s0, in_9, Serial_in_for_Left_Shift, out_12, out_13, n7474_2_p8

  // Notes on the sheet:
  //   4 Bit Universal Shift Register
  //   Parallel Output
  //   Parallel Input
endmodule
