// Logisim project 1905072.circ as structural Verilog: 1 circuit, main circuit main
module main (
  input  A,
  input  B,
  input  C,
  input  D,
  output out_5
);

  wire n7404_1_p2, n7404_1_p3, n7404_1_p11, n7404_1_p13, n7408_1_p3, n7408_1_p11, n7408_1_p14, n7408_1_p16,
       n7408_2_p3, n7408_2_p5, n7432_1_p8;

  // _7404 7404_1: pin names not known; wires that end beside it: 1'b1, n7404_1_p2, n7404_1_p3, B, n7404_1_p3, A, n7404_1_p2, 1'b0, 1'b1, C, n7404_1_p11, n7404_1_p11, n7404_1_p13
  // _7408 7408_1: pin names not known; wires that end beside it: n7404_1_p2, n7404_1_p3, n7408_1_p3, n7408_1_p3, n7404_1_p11, n7404_1_p13, 1'b0, 1'b1, A, B, n7408_1_p11, n7408_1_p11, D, n7408_1_p14, n7408_1_p14, n7408_1_p16
  // _7408 7408_2: pin names not known; wires that end beside it: A, C, n7408_2_p3, n7408_2_p3, n7408_2_p5, n7408_1_p16, 1'b0, 1'b1
  // _7432 7432_1: pin names not known; wires that end beside it: B, D, n7408_2_p5, 1'b0, 1'b1, n7404_1_p13, n7408_1_p14, n7432_1_p8, n7432_1_p8, n7408_1_p16, out_5, 1'b0

  // Notes on the sheet:
  //   B'
  //   A'
  //   C'
  //   A'B'C
  //   ABD
  //   AC(B+D)
  //   B+D
  //   A'B'C'+ABD+AC(B+D)
endmodule
