// Logisim project 1905072.circ as structural Verilog: 1 circuit, main circuit main
module main (
  input  w,
  input  x,
  input  y,
  input  z,
  output out_5
);

  wire n7408_1_p3, n7408_1_p6, n7408_1_p9, n74138_1_p8, n74138_1_p9, n74138_1_p10, n74138_2_p9, n74138_2_p10;

  // _74138 74138_1: pin names not known; wires that end beside it: z, y, x, w, 1'b0, 1'b1, 1'b1, n74138_1_p8, n74138_1_p9, n74138_1_p10
  // _74138 74138_2: pin names not known; wires that end beside it: 1'b0, z, y, x, 1'b0, 1'b0, w, 1'b1, n74138_2_p9, n74138_2_p10
  // _7404 7404_1: pin names not known; wires that end beside it: 1'b0, 1'b0, 1'b1
  // _7408 7408_1: pin names not known; wires that end beside it: n74138_1_p8, n74138_1_p9, n7408_1_p3, n7408_1_p3, n74138_1_p10, n7408_1_p6, 1'b0, 1'b1, n7408_1_p9, n74138_2_p10, out_5, n74138_2_p9, n7408_1_p6, n7408_1_p9
endmodule
