// Logisim project Test.circ as structural Verilog: 2 circuits, main circuit main
module main (
  input  w,
  input  x,
  input  y,
  input  z,
  output out_5
);

  wire n7408_1_p3, n7408_1_p6, n7408_1_p9, n74138_1_p7, n74138_1_p8, n74138_1_p9, n74138_2_p9, n74138_2_p10;

  // _74138 74138_1: pin names not known; wires that end beside it: z, y, x, w, 1'b0, 1'b1, n74138_1_p7, n74138_1_p8, n74138_1_p9
  // _74138 74138_2: pin names not known; wires that end beside it: 1'b0, z, y, x, 1'b0, 1'b0, w, 1'b1, n74138_2_p9, n74138_2_p10
  // _7404 7404_1: pin names not known; wires that end beside it: 1'b0, 1'b0, 1'b1
  // _7408 7408_1: pin names not known; wires that end beside it: n74138_1_p7, n74138_1_p8, n7408_1_p3, n7408_1_p3, n74138_1_p9, n7408_1_p6, 1'b0, 1'b1, n7408_1_p9, n74138_2_p10, out_5, n74138_2_p9, n7408_1_p6, n7408_1_p9
endmodule

module PE (
  input  I3,
  input  I2,
  input  I1,
  input  I0,
  output x,
  output out_6,
  output out_7
);

  wire n7432_1_p3, n7432_1_p6, n7432_1_p9, n7432_2_p3;

  // _7432 7432_1: pin names not known; wires that end beside it: I2, I0, n7432_1_p3, I0, I1, n7432_1_p6, 1'b0, 1'b1, n7432_1_p9, I2, x
  // _7404 7404_1: pin names not known; wires that end beside it: n7432_1_p3, out_6, n7432_1_p6, n7432_1_p9, 1'b0, 1'b1
  // _7432 7432_2: pin names not known; wires that end beside it: I3, I2, n7432_2_p3, n7432_2_p3, n7432_1_p6, out_7, 1'b0, 1'b1
endmodule
