// Logisim project 1905072.circ as structural Verilog: 1 circuit, main circuit main
module main (
  input  A,
  input  B,
  input  C,
  input  D,
  output Y
);

  wire n74153_1_p3, n74153_1_p7, n74153_1_p10, n74153_1_p16;

  // _74153 74153_1: pin names not known; wires that end beside it: A, B, n74153_1_p3, 1'b1, n74153_1_p3, 1'b0, n74153_1_p7, 1'b0, 1'b1, n74153_1_p10, C, 1'b0, D, 1'b1, D, n74153_1_p16
  // _7404 7404_1: pin names not known; wires that end beside it: A, n74153_1_p10, D, n74153_1_p3, 1'b0, 1'b1
  // _7432 7432_1: pin names not known; wires that end beside it: 1'b0, 1'b1, n74153_1_p7, n74153_1_p16, Y

  // Notes on the sheet:
  //   S1
  //   S2
  //   S0
  //   I1
  //   I4
  //   I5
  //   I0
  //   I2
  //   I3
  //   I6
  //   I7
endmodule
