// Logisim project Practice.circ as structural Verilog: 6 circuits, main circuit main
module main (
  input  A,
  input  B,
  input  C,
  input  D,
  output Y
);

  wire n74153_1_p3, n74153_1_p7, n74153_1_p10, n74153_1_p16;

  // _74153 74153_1: pin names not known; wires that end beside it: A, B, n74153_1_p3, 1'b1, n74153_1_p3, 1'b0, n74153_1_p7, 1'b0, 1'b1, n74153_1_p10, C, 1'b0, D, 1'b1, D, n74153_1_p16
  // _7404 7404_1: pin names not known; wires that end beside it: A, n74153_1_p10, D, n74153_1_p3, 1'b0, 1'b1
  // _7432 7432_1: pin names not known; wires that end beside it: 1'b0, 1'b1, n74153_1_p7, n74153_1_p16, Y

  // Notes on the sheet:
  //   S1
  //   S2
  //   S0
  //   I1
  //   I4
  //   I5
  //   I0
  //   I2
  //   I3
  //   I6
  //   I7
endmodule

module MUX (
  input  A,
  input  B,
  input  C,
  input  D,
  output out_5
);

  wire n74153_1_p11, n74153_1_p20, not_1_out, not_2_out;

  not not_1 (not_1_out, A);
  not not_2 (not_2_out, D);
  // _74153 74153_1: pin names not known; wires that end beside it: A, B, C, D, A, B, D, not_2_out, D, 1'b0, n74153_1_p11, 1'b0, 1'b1, not_1_out, C, 1'b0, 1'b0, 1'b1, D, n74153_1_p20
  // _74157 74157_1: pin names not known; wires that end beside it: A, n74153_1_p11, n74153_1_p20, out_5, 1'b0, 1'b1, 1'b0
endmodule

module MUX_2 (
  input  A,
  input  B,
  input  C,
  input  D,
  output Y
);

  wire n74153_1_p3, n74153_1_p7, n74153_1_p10, n74153_1_p16;

  // _74153 74153_1: pin names not known; wires that end beside it: A, B, n74153_1_p3, 1'b1, n74153_1_p3, 1'b0, n74153_1_p7, 1'b0, 1'b1, n74153_1_p10, C, 1'b0, D, 1'b1, D, n74153_1_p16
  // _7404 7404_1: pin names not known; wires that end beside it: A, n74153_1_p10, D, n74153_1_p3, 1'b0, 1'b1
  // _7432 7432_1: pin names not known; wires that end beside it: 1'b0, 1'b1, n74153_1_p7, n74153_1_p16, Y

  // Notes on the sheet:
  //   S1
  //   S2
  //   S0
  //   I1
  //   I4
  //   I5
  //   I0
  //   I2
  //   I3
  //   I6
  //   I7
endmodule

module ff (
  input  A,
  input  B,
  input  C,
  input  D,
  output out_5
);

  MUX_2 mux_1 (.A(A), .Y(out_5));  // open: B, C, D

  assign B = A;
  assign C = A;
  assign D = A;
  // also tied to VCC on the sheet: A
endmodule

module _1MUX (
  input  A,
  input  B,
  input  C,
  input  D,
  output out_5
);

  wire n74153_1_p2, n74153_1_p3, n74153_1_p4, n74157_1_p11;

  // _74153 74153_1: pin names not known; wires that end beside it: 1'b0, n74153_1_p2, n74153_1_p3, n74153_1_p4, 1'b0, A, 1'b0, n74153_1_p2, n74153_1_p3, n74153_1_p4, out_5, 1'b0, 1'b1, 1'b1, B
  // _74157 74157_1: pin names not known; wires that end beside it: C, 1'b0, D, n74153_1_p4, D, 1'b1, n74153_1_p2, 1'b0, 1'b1, 1'b0, n74157_1_p11, D, n74153_1_p3
  not not_1 (n74157_1_p11, D);

  // Notes on the sheet:
  //   0
  //   C+D
  //   C xnor D
  //   CD
endmodule

module _81 (
  input  A,
  input  B,
  input  C,
  input  D,
  output F
);

  wire n74151_1_p1;

  // _74151 74151_1: pin names not known; wires that end beside it: n74151_1_p1, 1'b0, D, n74151_1_p1, F, 1'b0, 1'b0, 1'b1, D, 1'b1, 1'b0, 1'b0, C, B, A
  // _74157 74157_1: pin names not known; wires that end beside it: D, 1'b1, 1'b0, n74151_1_p1, 1'b0, 1'b1, 1'b0
endmodule
