// Logisim project 1905072.circ as structural Verilog: 1 circuit, main circuit main
module main (
  input  Preset,
  output MSB,
  output out_3,
  output LSB
);

  wire clock_1_out;

  Clock clock_1 (.out(clock_1_out));
  // _7476 7476_1: pin names not known; wires that end beside it: clock_1_out, Preset, 1'b1, LSB, 1'b1, LSB, 1'b1, out_3
  // _7476 7476_2: pin names not known; wires that end beside it: Preset, out_3, Preset, 1'b1, 1'b1, MSB, 1'b1

  // Notes on the sheet:
  //   Clk
endmodule
