// Logisim project Counters.circ as structural Verilog: 5 circuits, main circuit main
module main (
  input  S,
  input  J,
  input  K,
  input  R,
  input  S_2,
  input  J_2,
  input  R_2,
  input  K_2,
  input  in_9,
  input  in_10,
  input  D,
  input  T,
  input  in_13,
  output Q_prime,
  output Q_prime_2,
  output Q,
  output Q_2,
  output Q_3,
  output Q_4,
  output Q_prime_3,
  output Q_prime_4,
  output Q_5,
  output Q_prime_5,
  output Q_6,
  output Q_7,
  output Q_prime_6,
  output Q_prime_7
);

  wire and_1_out, and_2_out, and_3_out, and_4_out, clock_1_out, clock_2_out, clock_3_out, clock_4_out,
       clock_5_out, clock_6_out, clock_7_out, nand_1_out, nand_2_out, nand_3_out, nand_4_out, nand_7_out,
       nand_8_out, nand_9_out, nand_10_out, nand_11_out, nand_14_out, nand_15_out, nand_16_out, nand_17_out,
       nand_20_out, nand_21_out, not_1_out;

  Clock clock_1 (.out(clock_1_out));
  Clock clock_2 (.out(clock_2_out));
  Clock clock_3 (.out(clock_3_out));
  Clock clock_4 (.out(clock_4_out));
  and and_1 (and_1_out, S, clock_1_out);
  and and_2 (and_2_out, clock_1_out, R);
  nand nand_1 (nand_1_out, S_2, clock_2_out);
  nand nand_2 (nand_2_out, clock_2_out, R_2);
  not not_1 (not_1_out, D);
  nand nand_3 (nand_3_out, Q_prime_5, in_9, clock_3_out);
  nand nand_4 (nand_4_out, clock_3_out, Q_5, in_10);
  nor nor_1 (Q_prime, and_1_out, Q);
  nor nor_2 (Q, Q_prime, and_2_out);
  nand nand_5 (Q_3, nand_1_out, Q_prime_3);
  nand nand_6 (Q_prime_3, Q_3, nand_2_out);
  nand nand_7 (nand_7_out, D, clock_4_out);
  nand nand_8 (nand_8_out, clock_4_out, not_1_out);
  nand nand_9 (nand_9_out, nand_3_out, nand_10_out);
  nand nand_10 (nand_10_out, nand_9_out, nand_4_out);
  nand nand_11 (nand_11_out, clock_3_out, clock_3_out);
  nand nand_12 (Q_7, nand_7_out, Q_prime_7);
  nand nand_13 (Q_prime_7, Q_7, nand_8_out);
  Clock clock_5 (.out(clock_5_out));
  Clock clock_6 (.out(clock_6_out));
  nand nand_14 (nand_14_out, nand_9_out, nand_11_out);
  nand nand_15 (nand_15_out, nand_11_out, nand_10_out);
  and and_3 (and_3_out, Q_prime_2, J, clock_5_out);
  and and_4 (and_4_out, clock_5_out, K, Q_2);
  nand nand_16 (nand_16_out, Q_4, clock_6_out);
  nand nand_17 (nand_17_out, clock_6_out, Q_prime_4);
  nand nand_18 (Q_5, nand_14_out, Q_prime_5);
  nand nand_19 (Q_prime_5, Q_5, nand_15_out);
  Clock clock_7 (.out(clock_7_out));
  nand nand_20 (nand_20_out, Q_6, clock_7_out);
  nand nand_21 (nand_21_out, clock_7_out, in_13);
  nor nor_3 (Q_prime_2, and_3_out, Q_2);
  nor nor_4 (Q_2, Q_prime_2, and_4_out);
  nand nand_22 (Q_4, nand_16_out, Q_prime_4);
  nand nand_23 (Q_prime_4, Q_4, nand_17_out);
  nand nand_24 (Q_6, nand_20_out, in_13);
  nand nand_25 (in_13, Q_6, nand_21_out);

  assign Q_prime_6 = in_13;
endmodule

module _2BitBinaryCounter (
  output [1:0] out_1
);

  wire clock_1_out;

  Clock clock_1 (.out(clock_1_out));
  J_K_Flip_Flop j_k_ff_1 (.J(1'b1), .clk(clock_1_out), .K(1'b1), .Q(out_1[0]));  // open: Qn, preset, en, reset
  J_K_Flip_Flop j_k_ff_2 (.J(out_1[0]), .clk(clock_1_out), .K(out_1[0]), .Q(out_1[1]));  // open: Qn, preset, en, reset

  // Notes on the sheet:
  //   00 -> 01 -> 10 -> 11
endmodule

module SequenceCounter (
  input  in_1,
  input  in_2,
  input  in_3
);

  wire and_1_out, and_2_out, and_3_out, clock_1_out, clock_2_out, n7474_1_p2, n7474_1_p5, n7474_1_p6,
       n7474_1_p8, n7474_1_p11, n7474_1_p12, n7474_2_p2, n7474_2_p5, n7474_2_p6, xnor_1_out, xnor_2_out;

  // _7408 7408_1: pin names not known
  // _7432 7432_1: pin names not known
  Clock clock_1 (.out(clock_1_out));
  Clock clock_2 (.out(clock_2_out));
  // _7474 7474_1: pin names not known; wires that end beside it: clock_1_out, n7474_1_p2, clock_2_out, in_1, n7474_1_p5, n7474_1_p6, clock_1_out, n7474_1_p8, clock_2_out, in_2, n7474_1_p11, n7474_1_p12
  // _7474 7474_2: pin names not known; wires that end beside it: clock_1_out, n7474_2_p2, clock_2_out, in_3, n7474_2_p5, n7474_2_p6
  or or_1 (n7474_1_p2, xnor_1_out, and_1_out);
  and and_1 (and_1_out, n7474_2_p6, n7474_1_p12);
  and and_2 (and_2_out, n7474_1_p11, n7474_1_p6);
  xnor xnor_1 (xnor_1_out, n7474_1_p11, n7474_1_p5);
  xnor xnor_2 (xnor_2_out, n7474_1_p11, n7474_1_p11);
  or or_2 (n7474_1_p8, and_3_out, n7474_1_p12);
  or or_3 (n7474_2_p2, and_2_out, xnor_2_out);
  and and_3 (and_3_out, n7474_2_p6, n7474_1_p6);

  // Notes on the sheet:
  //   2-3-4-6-1-7-5
  //   y2
  //   y1
  //   y0
endmodule

module dasd (
  input  in_1,
  input  in_2,
  input  in_3,
  output out_4,
  output out_5,
  output out_6
);

  wire clock_1_out, clock_2_out, n7408_1_p1, n7408_1_p2, n7408_1_p3, n7408_1_p6, n7408_1_p8, n7408_1_p9,
       n7408_2_p4, n7408_2_p7, n7432_1_p2, n7432_1_p3, n7432_1_p6, n7432_1_p7, n7432_2_p3, n7474_1_p2;

  // _7408 7408_1: pin names not known; wires that end beside it: n7408_1_p1, n7408_1_p2, n7408_1_p3, out_5, out_6, n7408_1_p6, n7408_1_p2, n7408_1_p8, n7408_1_p9
  // _7432 7432_1: pin names not known; wires that end beside it: n7408_1_p3, n7432_1_p2, n7432_1_p3, n7408_1_p9, n7408_1_p1, n7432_1_p6, n7432_1_p7, n7408_1_p6, n7432_1_p2
  Clock clock_1 (.out(clock_1_out));
  Clock clock_2 (.out(clock_2_out));
  // _7474 7474_1: pin names not known; wires that end beside it: clock_1_out, n7474_1_p2, clock_2_out, in_3, out_6, n7408_1_p2, clock_1_out, n7432_1_p6, clock_2_out, in_2, out_5, n7408_1_p1, n7408_1_p8, n7408_1_p1
  // _7474 7474_2: pin names not known; wires that end beside it: clock_1_out, n7432_1_p3, clock_2_out, in_1, out_4, n7408_1_p8
  // _7408 7408_2: pin names not known; wires that end beside it: n7408_1_p2, out_4, out_5, n7408_2_p4, out_5, n7408_1_p2, n7408_2_p7, n7408_1_p8, n7408_1_p1, n7432_1_p7
  // _7432 7432_2: pin names not known; wires that end beside it: n7408_2_p4, n7408_2_p7, n7432_2_p3, n7432_2_p3, n7432_1_p7, n7474_1_p2

  // Notes on the sheet:
  //   2-3-4-6-1-7-5
  //   y2'
  //   y2
  //   y0'
  //   y1'
  //   y1
  //   y0
  //   D0=y2y1+y1y0'+y2'y1'
  //   D1=y1'+y2'y0'
  //   D2=y1y0+y2'y1'+y1'y0'
endmodule

module JK (
  output y2,
  output y1,
  output y0
);

  wire clock_1_out, clock_2_out, clock_3_out, n7408_2_p1, n7432_1_p2, n7432_1_p4, n7432_1_p6, n7476_1_p5,
       n7476_1_p7, n7476_1_p8, n7476_1_p9, n7476_1_p10, n7476_2_p8;

  Clock clock_1 (.out(clock_1_out));
  Clock clock_2 (.out(clock_2_out));
  Clock clock_3 (.out(clock_3_out));
  // _7476 7476_1: pin names not known; wires that end beside it: clock_2_out, clock_1_out, clock_3_out, y1, n7476_1_p5, y0, n7476_1_p7, n7476_1_p8, n7476_1_p9, n7476_1_p10
  // _7476 7476_2: pin names not known; wires that end beside it: clock_2_out, clock_3_out, clock_2_out, clock_3_out, y1, n7476_1_p10, 1'b1, n7476_2_p8, y2, n7476_1_p9, y0, y2, n7476_1_p9, y1, n7476_1_p10, y0, n7476_1_p7
  // _7408 7408_1: pin names not known; wires that end beside it: n7476_1_p7, n7476_1_p9
  // _7432 7432_1: pin names not known; wires that end beside it: y1, n7432_1_p2, n7432_1_p2, n7432_1_p4, n7476_1_p5, n7432_1_p6, y0, y2, n7476_1_p8
  // _7408 7408_2: pin names not known; wires that end beside it: n7408_2_p1, n7476_2_p8, y2, n7476_1_p10, n7432_1_p4, n7476_1_p10, y0, n7432_1_p6, y1, n7476_1_p7, n7408_2_p1

  // Notes on the sheet:
  //   2-3-4-6-1-7-5
  //   y2'
  //   y1'
  //   y0'
endmodule
